# Fritzing sketch CircuitDiagram (saved by Fritzing 0.9.3b)
breadboards: 1

parts:
  hc-sr1 = hc-sr04
  LED1 = LED - 3mm [color="Red (633nm)" package="3 mm [THT]"]
  LED2 = LED - 3mm [color="Red (633nm)" package="3 mm [THT]"]
  LED3 = LED - 3mm [color="Red (633nm)" package="3 mm [THT]"]
  T1 = LM35 Temperature Sensor [package="TO92 [THT]"]
  Componente2 = Arduino Uno (Rev3)
  R1 = Resistor [tolerance=±5% resistance=220 package=THT]
  R2 = Resistor [tolerance=±5% resistance=220 package=THT]
  R3 = Resistor [tolerance=±5% resistance=220 package=THT]

nets:
  VCC: hc-sr1.VCC, T1.+Vs, Componente2.5V
  N1: hc-sr1.Trig, Componente2.D9_PWM
  N2: hc-sr1.Echo, Componente2.D8
  GND: hc-sr1.GND, T1.GND, Componente2.GND, R1.Pin_1, R2.Pin_1, R3.Pin_1
  N3: LED1.cathode, R3.Pin_0
  N4: LED1.anode, Componente2.D10_PWM/SS
  N5: LED2.cathode, R2.Pin_0
  N6: LED2.anode, Componente2.D12/MISO
  N7: LED3.cathode, R1.Pin_0
  N8: LED3.anode, Componente2.D13/SCK
  N9: T1.Vout, Componente2.A0
